// Logisim project HalfAdder_FullAdder_Circuit.circ as structural Verilog: 6 circuits, main circuit 8-bit adder
module _8_bit_adder (
  input  [7:0] a,
  input  [7:0] b,
  output [7:0] out_3,
  output carry
);

  wire full_adder_1_cout, full_adder_2_cout, full_adder_3_cout, full_adder_4_cout, full_adder_5_cout,
       full_adder_6_cout, full_adder_7_cout;

  Full_Adder full_adder_1 (.A(1'b0), .B(a[0]), .Cin(b[0]), .Sum(out_3[0]), .Cout(full_adder_1_cout));
  Full_Adder full_adder_2 (.A(full_adder_1_cout), .B(a[1]), .Cin(b[1]), .Sum(out_3[1]), .Cout(full_adder_2_cout));
  Full_Adder full_adder_3 (.A(full_adder_2_cout), .B(a[2]), .Cin(b[2]), .Sum(out_3[2]), .Cout(full_adder_3_cout));
  Full_Adder full_adder_4 (.A(full_adder_3_cout), .B(a[3]), .Cin(b[3]), .Sum(out_3[3]), .Cout(full_adder_4_cout));
  Full_Adder full_adder_5 (.A(full_adder_4_cout), .B(a[4]), .Cin(b[4]), .Sum(out_3[4]), .Cout(full_adder_5_cout));
  Full_Adder full_adder_6 (.A(full_adder_5_cout), .B(a[5]), .Cin(b[5]), .Sum(out_3[5]), .Cout(full_adder_6_cout));
  Full_Adder full_adder_7 (.A(full_adder_6_cout), .B(a[6]), .Cin(b[6]), .Sum(out_3[6]), .Cout(full_adder_7_cout));
  Full_Adder full_adder_8 (.A(full_adder_7_cout), .B(a[7]), .Cin(b[7]), .Sum(out_3[7]), .Cout(carry));
endmodule

module Half_Adder (
  input  A,
  input  B,
  output Sum,
  output Carry
);

  xor xor_1 (Sum, A, B);
  and and_1 (Carry, A, B);
endmodule

// fa
module Full_Adder (
  input  A,
  input  B,
  input  Cin,
  output Sum,
  output Cout
);

  wire half_adder_1_carry, half_adder_1_sum, half_adder_2_carry;

  Half_Adder half_adder_1 (.A(A), .B(B), .Sum(half_adder_1_sum), .Carry(half_adder_1_carry));
  Half_Adder half_adder_2 (.A(half_adder_1_sum), .B(Cin), .Sum(Sum), .Carry(half_adder_2_carry));
  or or_1 (Cout, half_adder_2_carry, half_adder_1_carry);
endmodule

module _8_bit_ALU (
  input  [7:0] in_1,
  input  [7:0] in_2,
  input  [2:0] in_3,
  output [7:0] out_4,
  output out_5
);

  wire undriven;
  wire [7:0] and_1_out, n8_bit_adder_1_out_3, nor_1_out, or_1_out, slt_1_out_3, subtractor_1_out, xnor_1_out,
       xor_1_out;

  assign and_1_out = in_1 & in_2;  // AND_Gate and_1, 8 bits wide
  assign or_1_out = in_1 | in_2;  // OR_Gate or_1, 8 bits wide
  _8_bit_adder u_8_bit_adder_1 (.a(in_1), .b(in_2), .out_3(n8_bit_adder_1_out_3));  // open: carry
  Subtractor subtractor_1 (.a(in_1), .b(in_2), .out(subtractor_1_out));  // open: bin, bout
  slt slt_1 (.in_1(in_1), .in_2(in_2), .out_3(slt_1_out_3));
  assign xor_1_out = in_1 ^ in_2;  // XOR_Gate xor_1, 8 bits wide
  assign xnor_1_out = ~(in_1 ^ in_2);  // XNOR_Gate xnor_1, 8 bits wide
  assign nor_1_out = ~(in_1 | in_2);  // NOR_Gate nor_1, 8 bits wide
  Multiplexer #(.select(3), .width(8)) multiplexer_1 (
    .in0(and_1_out), .in1(or_1_out), .in2(n8_bit_adder_1_out_3), .in3(subtractor_1_out), .in4(slt_1_out_3),
    .in5(xor_1_out), .in6(xnor_1_out), .in7(nor_1_out), .out(out_4), .sel(in_3), .en(undriven));
  Comparator comparator_1 (.a(out_4), .b({8{1'b0}}), .eq(out_5));  // open: gt, lt
endmodule

module slt (
  input  [7:0] in_1,
  input  [7:0] in_2,
  output [7:0] out_3
);

  wire [7:0] subtractor_1_out;

  Subtractor subtractor_1 (.a(in_1), .b(in_2), .out(subtractor_1_out));  // open: bin, bout
  Shifter #(.shift("lr")) shifter_1 (.in(subtractor_1_out), .\dist (3'b111), .out(out_3));
endmodule

module main (
  input  [7:0] in_1,
  input  [7:0] in_2,
  input  [2:0] in_3,
  output [7:0] out_4,
  output out_5
);

  _8_bit_ALU u_8_bit_alu_1 (.in_1(in_1), .in_2(in_2), .in_3(in_3), .out_4(out_4), .out_5(out_5));
endmodule
