// Logisim project MIPS_Circuit.circ as structural Verilog: 11 circuits, main circuit 8-bit adder
module main (
  input  [7:0] in_1,
  input  [7:0] in_2,
  input  [2:0] in_3,
  output [7:0] out_4,
  output out_5
);

  _8_bit_ALU u_8_bit_alu_1 (.a(in_1), .b(in_2), .in_3(in_3), .result(out_4), .out_5(out_5));
endmodule

module Half_Adder (
  input  [7:0] A,
  input  [7:0] B,
  output [7:0] Sum,
  output [7:0] Carry
);

  assign Sum = A ^ B;  // XOR_Gate xor_1, 8 bits wide
  assign Carry = A & B;  // AND_Gate and_1, 8 bits wide
endmodule

// fa
module Full_Adder (
  input  [7:0] A,
  input  [7:0] B,
  input  [7:0] Cin,
  output [7:0] Sum,
  output [7:0] Cout
);

  wire [7:0] half_adder_1_carry, half_adder_1_sum, half_adder_2_carry;

  Half_Adder half_adder_1 (.A(A), .B(B), .Sum(half_adder_1_sum), .Carry(half_adder_1_carry));
  Half_Adder half_adder_2 (.A(half_adder_1_sum), .B(Cin), .Sum(Sum), .Carry(half_adder_2_carry));
  assign Cout = half_adder_2_carry | half_adder_1_carry;  // OR_Gate or_1, 8 bits wide
endmodule

module _8_bit_adder (
  input  [7:0] a,
  input  [7:0] b,
  output [7:0] out_3,
  output [7:0] carry
);

  wire [7:0] full_adder_1_cout, full_adder_2_cout, full_adder_3_cout, full_adder_4_cout, full_adder_5_cout,
       full_adder_6_cout, full_adder_7_cout;

  Full_Adder full_adder_1 (.A({8{1'b0}}), .B(a), .Cin(b), .Sum(out_3), .Cout(full_adder_1_cout));
  Full_Adder full_adder_2 (.A(full_adder_1_cout), .B(a), .Cin(b), .Sum(out_3), .Cout(full_adder_2_cout));
  Full_Adder full_adder_3 (.A(full_adder_2_cout), .B(a), .Cin(b), .Sum(out_3), .Cout(full_adder_3_cout));
  Full_Adder full_adder_4 (.A(full_adder_3_cout), .B(a), .Cin(b), .Sum(out_3), .Cout(full_adder_4_cout));
  Full_Adder full_adder_5 (.A(full_adder_4_cout), .B(a), .Cin(b), .Sum(out_3), .Cout(full_adder_5_cout));
  Full_Adder full_adder_6 (.A(full_adder_5_cout), .B(a), .Cin(b), .Sum(out_3), .Cout(full_adder_6_cout));
  Full_Adder full_adder_7 (.A(full_adder_6_cout), .B(a), .Cin(b), .Sum(out_3), .Cout(full_adder_7_cout));
  Full_Adder full_adder_8 (.A(full_adder_7_cout), .B(a), .Cin(b), .Sum(out_3), .Cout(carry));
endmodule

module slt (
  input  [7:0] in_1,
  input  [7:0] in_2,
  output [7:0] out_3
);

  wire [7:0] subtractor_1_out;

  Subtractor subtractor_1 (.a(in_1), .b(in_2), .out(subtractor_1_out));  // open: bin, bout
  Shifter #(.shift("lr")) shifter_1 (.in(subtractor_1_out), .\dist (3'b111), .out(out_3));
endmodule

module _8_bit_ALU (
  input  [7:0] a,
  input  [7:0] b,
  input  [2:0] in_3,
  output [7:0] result,
  output out_5
);

  wire undriven;
  wire [7:0] and_1_out, n8_bit_adder_1_out_3, nor_1_out, or_1_out, slt_1_out_3, subtractor_1_out, xnor_1_out,
       xor_1_out;

  assign and_1_out = a & b;  // AND_Gate and_1, 8 bits wide
  assign or_1_out = a | a;  // OR_Gate or_1, 8 bits wide
  _8_bit_adder u_8_bit_adder_1 (.a(a), .b(b), .out_3(n8_bit_adder_1_out_3));  // open: carry
  Subtractor subtractor_1 (.a(a), .b(a), .out(subtractor_1_out));  // open: bin, bout
  slt slt_1 (.in_1(a), .in_2(b), .out_3(slt_1_out_3));
  assign xor_1_out = a ^ a;  // XOR_Gate xor_1, 8 bits wide
  assign xnor_1_out = ~(a ^ b);  // XNOR_Gate xnor_1, 8 bits wide
  assign nor_1_out = ~(a | b);  // NOR_Gate nor_1, 8 bits wide
  Multiplexer #(.select(3), .width(8)) multiplexer_1 (
    .in0(and_1_out), .in1(or_1_out), .in2(n8_bit_adder_1_out_3), .in3(subtractor_1_out), .in4(slt_1_out_3),
    .in5(xor_1_out), .in6(xnor_1_out), .in7(nor_1_out), .out(result), .sel(in_3), .en(undriven));
  Comparator comparator_1 (.a(result), .b({8{1'b0}}), .eq(out_5));  // open: gt, lt
endmodule

module RegFile (
  input  [7:0] \input ,
  input  [2:0] read_adrr1,
  input  [2:0] read_adrr2,
  input  [2:0] write_adrr,
  input  write_enable,
  output [7:0] out_6,
  output [7:0] out_7
);

  wire clock_out, decoder_1_out0, decoder_1_out1, decoder_1_out2, decoder_1_out3, decoder_1_out4,
       decoder_1_out5, decoder_1_out6, decoder_1_out7;
  wire [7:0] register_1_q, register_2_q, register_3_q, register_4_q, register_5_q, register_6_q,
       register_7_q, register_8_q;

  Decoder #(.select(3), .disabled(0)) decoder_1 (
    .out0(decoder_1_out0), .out1(decoder_1_out1), .out2(decoder_1_out2), .out3(decoder_1_out3),
    .out4(decoder_1_out4), .out5(decoder_1_out5), .out6(decoder_1_out6), .out7(decoder_1_out7),
    .sel(write_adrr), .en(write_enable));
  Clock clock (.out(clock_out));
  Register register_1 (.D(\input ), .en(decoder_1_out0), .Q(register_1_q), .clk(clock_out));  // open: clr
  Register register_2 (.D(\input ), .en(decoder_1_out1), .Q(register_2_q), .clk(clock_out));  // open: clr
  Register register_3 (.D(\input ), .en(decoder_1_out2), .Q(register_3_q), .clk(clock_out));  // open: clr
  Register register_4 (.D(\input ), .en(decoder_1_out3), .Q(register_4_q), .clk(clock_out));  // open: clr
  Register register_5 (.D(\input ), .en(decoder_1_out4), .Q(register_5_q), .clk(clock_out));  // open: clr
  Register register_6 (.D(\input ), .en(decoder_1_out5), .Q(register_6_q), .clk(clock_out));  // open: clr
  Register register_7 (.D(\input ), .en(decoder_1_out6), .Q(register_7_q), .clk(clock_out));  // open: clr
  Register register_8 (.D(\input ), .en(decoder_1_out7), .Q(register_8_q), .clk(clock_out));  // open: clr
  Multiplexer #(.select(3), .width(8)) multiplexer_1 (
    .in0(register_1_q), .in1(register_2_q), .in2(register_3_q), .in3(register_4_q), .in4(register_5_q),
    .in5(register_6_q), .in6(register_7_q), .in7(register_8_q), .out(out_6), .sel(read_adrr1));  // open: en
  Multiplexer #(.select(3), .width(8)) multiplexer_2 (
    .in0(register_1_q), .in1(register_2_q), .in2(register_3_q), .in3(register_4_q), .in4(register_5_q),
    .in5(register_6_q), .in6(register_7_q), .in7(register_8_q), .out(out_7), .sel(read_adrr2));  // open: en
endmodule

module TestRegFile (
  input  [7:0] inputdate,
  input  [2:0] readress,
  input  [2:0] readress2,
  input  in_4,
  input  [2:0] writeadrress,
  output [7:0] readata,
  output [7:0] readata_2
);

  wire [2:0] undriven;

  RegFile regfile_1 (
    .\input (inputdate), .read_adrr1(readress), .read_adrr2(readress2), .write_adrr(writeadrress),
    .write_enable(in_4), .out_6(readata), .out_7(readata_2));
  _8_bit_ALU ALU (.a(readata), .b(readata_2), .in_3(undriven));  // open: result, out_5
endmodule

module controller (
  input  op3,
  input  op2,
  input  op1,
  input  op0,
  output RegDst,
  output ALUSrc,
  output Jump,
  output MemtoReg,
  output RegWrite,
  output MemRead,
  output MemWrite,
  output Branch,
  output ALUOp1,
  output ALUOp0
);

  wire not_1_out, not_2_out, not_3_out, not_4_out, not_5_out, not_6_out, not_7_out, not_8_out, not_9_out;

  not not_1 (not_1_out, op3);
  and and_1 (RegDst, not_1_out, not_2_out);
  not not_2 (not_2_out, op0);
  or or_1 (ALUSrc, op0, op3);
  not not_3 (not_3_out, op3);
  and and_2 (Jump, not_3_out, op1);
  not not_4 (not_4_out, op2);
  and and_3 (RegWrite, not_4_out, not_5_out);
  not not_5 (not_5_out, op1);
  not not_6 (not_6_out, op3);
  and and_4 (MemRead, not_6_out, op0);
  and and_5 (MemWrite, op3, op1);
  not not_7 (not_7_out, op3);
  not not_8 (not_8_out, op2);
  and and_6 (ALUOp1, not_7_out, not_8_out, not_9_out);
  not not_9 (not_9_out, op0);

  assign ALUOp0 = op2;
  assign Branch = op2;
  assign MemtoReg = op0;
endmodule

module ALUcontrol (
  input  ALUOp1,
  input  ALUOp0,
  input  Fun2,
  input  Fun1,
  input  Fun0,
  output ALUCont2,
  output ALUCont1,
  output ALUCont0
);

  wire and_2_out, not_1_out;

  and and_1 (ALUCont2, ALUOp1, Fun2);
  not not_1 (not_1_out, ALUOp1);
  and and_2 (and_2_out, ALUOp1, Fun0);
  or or_1 (ALUCont1, not_1_out, Fun1);
  or or_2 (ALUCont0, ALUOp0, and_2_out);
endmodule

module SMIPS_Datapath (
);

  wire ALU_out_5, and_1_out, clock_1_out, controller_1_aluop0, controller_1_aluop1, controller_1_alusrc,
       controller_1_branch, controller_1_jump, controller_1_memread, controller_1_memtoreg,
       controller_1_memwrite, controller_1_regdst, controller_1_regwrite, not_1_out;
  wire [2:0] alucontrol_1_alucont0, multiplexer_1_out;
  wire [7:0] adder_1_out, adder_2_out, ALU_result, multiplexer_2_out, multiplexer_4_out, multiplexer_5_out,
       PC_q, ram_1_data, RegFile_out_6, RegFile_out_7, undriven;
  wire [17:0] rom_1_data;

  Register PC (.D(multiplexer_4_out), .Q(PC_q), .clk(clock_1_out));  // open: en, clr
  Adder adder_1 (.a(PC_q), .out(adder_1_out));  // open: b, cin, cout
  ROM #(.dataWidth(18)) rom_1 (.addr(PC_q), .data(rom_1_data));  // open: sel
  Multiplexer #(.width(3)) multiplexer_1 (
    .in0(rom_1_data[10:8]), .in1(rom_1_data[7:5]), .out(multiplexer_1_out), .sel(controller_1_regdst));  // open: en
  controller controller_1 (
    .op3(rom_1_data[14]), .op2(rom_1_data[15]), .op1(rom_1_data[16]), .op0(rom_1_data[17]),
    .RegDst(controller_1_regdst), .ALUSrc(controller_1_alusrc), .Jump(controller_1_jump),
    .MemtoReg(controller_1_memtoreg), .RegWrite(controller_1_regwrite), .MemRead(controller_1_memread),
    .MemWrite(controller_1_memwrite), .Branch(controller_1_branch), .ALUOp1(controller_1_aluop1),
    .ALUOp0(controller_1_aluop0));
  RegFile RegFile (
    .\input (multiplexer_5_out), .read_adrr1(rom_1_data[13:11]), .read_adrr2(rom_1_data[10:8]),
    .write_adrr(multiplexer_1_out), .write_enable(controller_1_regwrite), .out_6(RegFile_out_6),
    .out_7(RegFile_out_7));
  Adder adder_2 (.a(adder_1_out), .b(rom_1_data[7:0]), .out(adder_2_out));  // open: cin, cout
  Multiplexer #(.width(8)) multiplexer_2 (
    .in0(RegFile_out_7), .in1(rom_1_data[7:0]), .out(multiplexer_2_out), .sel(controller_1_alusrc));  // open: en
  and and_1 (and_1_out, controller_1_branch, ALU_out_5);
  _8_bit_ALU ALU (
    .a(RegFile_out_6), .b(multiplexer_2_out), .in_3(alucontrol_1_alucont0), .result(ALU_result),
    .out_5(ALU_out_5));
  Multiplexer #(.width(8)) multiplexer_3 (.in0(adder_1_out), .in1(adder_2_out), .sel(and_1_out));  // open: out, en
  ALUcontrol alucontrol_1 (
    .ALUOp1(controller_1_aluop0), .ALUOp0(controller_1_aluop1), .Fun2(rom_1_data[2]), .Fun1(rom_1_data[1]),
    .Fun0(rom_1_data[0]), .ALUCont2(alucontrol_1_alucont0[2]), .ALUCont1(alucontrol_1_alucont0[1]),
    .ALUCont0(alucontrol_1_alucont0[0]));
  Multiplexer #(.width(8)) multiplexer_4 (
    .in0(undriven), .in1(rom_1_data[7:0]), .out(multiplexer_4_out), .sel(controller_1_jump));  // open: en
  Clock clock_1 (.out(clock_1_out));
  not not_1 (not_1_out, clock_1_out);
  RAM #(.bus("separate")) ram_1 (
    .addr(ALU_result), .din(RegFile_out_7), .data(ram_1_data), .str(controller_1_memwrite), .clk(not_1_out),
    .ld(controller_1_memread));  // open: sel, clr
  Multiplexer #(.width(8)) multiplexer_5 (
    .in0(ALU_result), .in1(ram_1_data), .out(multiplexer_5_out), .sel(controller_1_memtoreg));  // open: en
endmodule
